# Fritzing sketch scheme (saved by Fritzing 0.9.3b)
breadboards: 1

parts:
  Arduino_Attacker = Arduino Nano (Rev3.0) (ICSP)
  Arduino_Whack_a_Mole = Arduino Nano (Rev3.0) (ICSP)

nets:
  N1: Arduino_Attacker.D2, Arduino_Whack_a_Mole.D2
  N2: Arduino_Attacker.D3, Arduino_Whack_a_Mole.D3
  N3: Arduino_Attacker.D4, Arduino_Whack_a_Mole.D4
  N4: Arduino_Attacker.D5, Arduino_Whack_a_Mole.D5
  N5: Arduino_Attacker.D6, Arduino_Whack_a_Mole.D6
  N6: Arduino_Attacker.D7, Arduino_Whack_a_Mole.D7
  N7: Arduino_Attacker.D8, Arduino_Whack_a_Mole.D8
  N8: Arduino_Attacker.D9, Arduino_Whack_a_Mole.D9
  N9: Arduino_Attacker.D10, Arduino_Whack_a_Mole.D10
  N10: Arduino_Attacker.D11/MOSI, Arduino_Whack_a_Mole.D11/MOSI
  N11: Arduino_Attacker.D12/MISO, Arduino_Whack_a_Mole.D12/MISO
  N12: Arduino_Attacker.A5, Arduino_Whack_a_Mole.D1/TX
  N13: Arduino_Attacker.A4, Arduino_Whack_a_Mole.D0/RX
  N14: Arduino_Attacker.D13/SCK, Arduino_Whack_a_Mole.D13/SCK
